// Logisim project mips-like.circ as structural Verilog: 4 circuits, main circuit PROCESSADOR
module PROCESSADOR (
  output [31:0] \INSTRUÇÃO 
);

  wire branch, button_1_out, clock_1_out, jump, li, si, UC_branch, UC_write_reg, ula_1_bge;
  wire [1:0] UC_alu_op;
  wire [3:0] multiplexer_3_out;
  wire [7:0] PC_q_2;
  wire [31:0] adder_1_out, adder_2_out, banco_de_registradores_1_r0_d, banco_de_registradores_1_r1_d,
       bit_extender_1_out, bit_extender_2_out, multiplexer_1_out, multiplexer_2_out, multiplexer_4_out, PC_q,
       ram_1_data, ula_1_ula_out;

  Multiplexer #(.width(32), .enable("false")) multiplexer_1 (
    .in0(adder_1_out), .in1(adder_2_out), .out(multiplexer_1_out), .sel(branch));
  Adder #(.width(32)) adder_1 (.a({PC_q[31:10], PC_q_2, PC_q[1:0]}), .b(32'h4), .out(adder_1_out));  // open: cin, cout
  assign bit_extender_1_out = {{4{1'b0}}, \INSTRUÇÃO [27:0]};  // Bit_Extender bit_extender_1
  Multiplexer #(.width(32), .enable("false")) multiplexer_2 (
    .in0(multiplexer_1_out), .in1(bit_extender_1_out), .out(multiplexer_2_out), .sel(jump));
  assign bit_extender_2_out = {{16{1'b0}}, \INSTRUÇÃO [15:0]};  // Bit_Extender bit_extender_2
  Register #(.width(32)) PC (
    .D(multiplexer_2_out), .Q({PC_q[31:10], PC_q_2, PC_q[1:0]}), .clk(clock_1_out), .clr(button_1_out));  // open: en
  Clock clock_1 (.out(clock_1_out));
  Button button_1 (.out(button_1_out));
  Adder #(.width(32)) adder_2 (.a(bit_extender_2_out), .b(adder_1_out), .out(adder_2_out));  // open: cin, cout
  ROM #(.dataWidth(32)) rom_1 (.addr(PC_q_2), .data(\INSTRUÇÃO ));  // open: sel
  UC UC (
    .E3(\INSTRUÇÃO [31]), .E2(\INSTRUÇÃO [30]), .E1(\INSTRUÇÃO [29]), .E0(\INSTRUÇÃO [28]),
    .write_reg(UC_write_reg), .read_mem(li), .alu_op(UC_alu_op), .write_mem(si), .jump(jump),
    .branch(UC_branch));
  Multiplexer #(.width(4), .enable("false")) multiplexer_3 (
    .in0(\INSTRUÇÃO [19:16]), .in1(\INSTRUÇÃO [27:24]), .out(multiplexer_3_out), .sel(si));
  BANCO_DE_REGISTRADORES banco_de_registradores_1 (
    .DATA_WRITE(multiplexer_4_out), .CLK(clock_1_out), .RW(\INSTRUÇÃO [27:24]),
    .R0_D(banco_de_registradores_1_r0_d), .R0(multiplexer_3_out), .R1_D(banco_de_registradores_1_r1_d),
    .R1(\INSTRUÇÃO [23:20]), .RW_2(UC_write_reg), .RESET(button_1_out));
  ULA ula_1 (
    .DATA_0(banco_de_registradores_1_r0_d), .DATA_1(banco_de_registradores_1_r1_d), .ULA_OUT(ula_1_ula_out),
    .ULA_OP(UC_alu_op), .branch(UC_branch), .bge(ula_1_bge));
  and and_1 (branch, UC_branch, ula_1_bge);
  Multiplexer #(.width(32), .enable("false")) multiplexer_4 (
    .in0(ula_1_ula_out), .in1(ram_1_data), .out(multiplexer_4_out), .sel(li));
  RAM #(.dataWidth(32), .bus("separate")) ram_1 (
    .addr(\INSTRUÇÃO [23:16]), .din(banco_de_registradores_1_r0_d), .data(ram_1_data), .str(si),
    .clk(clock_1_out), .ld(li));  // open: sel, clr

  // Notes on the sheet:
  //   contents of rom_1 (hex, n*v repeats v):
  //   30000000 40010000 1000000 90010000 90000008 80000000 80000000 80000020
  //   REG_0
  //   REG_1
  //   REG_W
  //   DATA_W
  //   BANCO DE REGISTRADORES
  //   REG0_D
  //   REG1_D
  //   ULA
endmodule

module ULA (
  input  [31:0] DATA_0,
  input  [31:0] DATA_1,
  input  [1:0] ULA_OP,
  input  branch,
  output [31:0] ULA_OUT,
  output bge
);

  wire and_1_out, and_2_out, comparator_1_eq, comparator_1_gt;
  wire [31:0] adder_1_out, multiplier_1_out, subtractor_1_out;

  Comparator #(.width(32), .mode("unsigned")) comparator_1 (
    .a(DATA_0), .b(DATA_1), .gt(comparator_1_gt), .eq(comparator_1_eq));  // open: lt
  and and_1 (and_1_out, comparator_1_gt, branch);
  and and_2 (and_2_out, comparator_1_eq, branch);
  Adder #(.width(32)) adder_1 (.a(DATA_0), .b(DATA_1), .out(adder_1_out));  // open: cin, cout
  Subtractor #(.width(32)) subtractor_1 (.a(DATA_0), .b(DATA_1), .out(subtractor_1_out));  // open: bin, bout
  Multiplier #(.width(32)) multiplier_1 (.a(DATA_0), .b(DATA_1), .out(multiplier_1_out));  // open: cin, cout
  or or_1 (bge, and_1_out, and_2_out);
  Multiplexer #(.select(2), .width(32), .enable("false")) multiplexer_1 (
    .in0(adder_1_out), .in1(subtractor_1_out), .in2(multiplier_1_out), .out(ULA_OUT), .sel(ULA_OP));  // open: in3
endmodule

module UC (
  input  E3,
  input  E2,
  input  E1,
  input  E0,
  output write_reg,
  output read_mem,
  output [1:0] alu_op,
  output write_mem,
  output jump,
  output branch
);

  wire not_1_out, not_2_out, not_3_out, not_4_out, not_5_out, not_6_out, not_7_out, not_8_out, not_9_out,
       not_10_out, not_11_out, not_12_out;
  wire [1:0] multiplexer_1_out;

  not not_1 (not_1_out, E3);
  not not_2 (not_2_out, E2);
  not not_3 (not_3_out, E3);
  not not_4 (not_4_out, E2);
  not not_5 (not_5_out, E3);
  not not_6 (not_6_out, E1);
  not not_7 (not_7_out, E0);
  not not_8 (not_8_out, E2);
  not not_9 (not_9_out, E1);
  not not_10 (not_10_out, E0);
  not not_11 (not_11_out, E2);
  not not_12 (not_12_out, E1);
  and and_1 (write_reg, not_1_out, not_2_out);
  and and_2 (read_mem, not_3_out, not_4_out, E1, E0);
  and and_3 (write_mem, not_5_out, E2, not_6_out, not_7_out);
  and and_4 (jump, E3, not_8_out, not_9_out, not_10_out);
  and and_5 (branch, E3, not_11_out, not_12_out, E0);
  Multiplexer #(.width(2), .enable("false")) multiplexer_1 (
    .in0(2'b00), .in1(2'b01), .out(multiplexer_1_out), .sel(E0));
  Multiplexer #(.width(2), .enable("false")) multiplexer_2 (
    .in0(multiplexer_1_out), .in1(2'b10), .out(alu_op), .sel(E1));
endmodule

module BANCO_DE_REGISTRADORES (
  input  [31:0] DATA_WRITE,
  input  [3:0] R0,
  input  CLK,
  input  [3:0] R1,
  input  [3:0] RW,
  input  RESET,
  input  RW_2,
  output [31:0] R0_D,
  output [31:0] R1_D
);

  wire demultiplexer_1_out0, demultiplexer_1_out1, demultiplexer_1_out2, demultiplexer_1_out3;
  wire [31:0] register_1_q, register_2_q, register_3_q, register_4_q;

  Demultiplexer #(.select(2), .enable("false")) demultiplexer_1 (
    .out0(demultiplexer_1_out0), .out1(demultiplexer_1_out1), .out2(demultiplexer_1_out2),
    .out3(demultiplexer_1_out3), .in(RW_2), .sel(RW[1:0]));
  Register #(.width(32)) register_1 (
    .D(DATA_WRITE), .en(demultiplexer_1_out0), .Q(register_1_q), .clk(CLK), .clr(RESET));
  Register #(.width(32)) register_2 (
    .D(DATA_WRITE), .en(demultiplexer_1_out1), .Q(register_2_q), .clk(CLK), .clr(RESET));
  Register #(.width(32)) register_3 (
    .D(DATA_WRITE), .en(demultiplexer_1_out2), .Q(register_3_q), .clk(CLK), .clr(RESET));
  Register #(.width(32)) register_4 (
    .D(DATA_WRITE), .en(demultiplexer_1_out3), .Q(register_4_q), .clk(CLK), .clr(RESET));
  Multiplexer #(.select(2), .width(32), .disabled(0), .enable("false")) multiplexer_1 (
    .in0(register_1_q), .in1(register_2_q), .in2(register_3_q), .in3(register_4_q), .out(R0_D), .sel(R0[1:0]));
  Multiplexer #(.select(2), .width(32), .enable("false")) multiplexer_2 (
    .in0(register_1_q), .in1(register_2_q), .in2(register_3_q), .in3(register_4_q), .out(R1_D), .sel(R1[1:0]));
endmodule
